# Fritzing sketch WemosD1R2mini_TFT2 (saved by Fritzing 0.9.3b)
breadboards: 1

parts:
  WeMos_D1_Mini1 = WeMos D1 Mini
  U1 = 2.4" TFT LCD screen, SPI, Touch-enabled

nets:
  N1: WeMos_D1_Mini1.5V, U1.LED
  N2: WeMos_D1_Mini1.D1, U1.T_IRQ
  N3: WeMos_D1_Mini1.D2, U1.T_CS
  N4: WeMos_D1_Mini1.D3, U1.DC
  N5: WeMos_D1_Mini1.D5, U1.T_CLK, U1.SCL
  N6: WeMos_D1_Mini1.D6, U1.T_DO
  N7: WeMos_D1_Mini1.D7, U1.T_DIN, U1.SDA
  N8: WeMos_D1_Mini1.D8, U1.CS
  N9: WeMos_D1_Mini1.G, U1.GND
  N10: U1.RESET, U1.VCC

custom parts:
  WeMos D1 Mini: The D1 mini is a mini wifi board based on ESP-8266EX.
  2.4" TFT LCD screen, SPI, Touch-enabled: 2.4", ILI9341-based TFT LCD screen with touch-sensing using the XPT2046 controller, SPI-compatible. There is also an SD-card version that is non-touch enabled but uses exactly the same board and pinout. This part is for both, though it should be noted that the SD reader and the touch screen are mutually incompatible
